// Logisim project lab8.circ as structural Verilog: 1 circuit, main circuit main
module main (
  input  X,
  input  Y,
  input  Z,
  output out_4,
  output out_5
);

  wire and_1_out, and_2_out, xor_1_out;

  xor xor_1 (xor_1_out, X, Y);
  and and_1 (and_1_out, X, Y);
  xor xor_2 (out_4, xor_1_out, Z);
  and and_2 (and_2_out, xor_1_out, Z);
  or or_1 (out_5, and_2_out, and_1_out);
endmodule
